// Logisim project Cavalleri_Emanuele_908838_arch1lab_progetto.circ as structural Verilog: 6 circuits, main circuit main
module main (
);

  wire button_1_out, button_2_out, button_3_out, button_4_out, button_5_out, button_6_out, button_7_out,
       button_8_out, button_9_out, O, RESET_SCORE_out, START_RESET_out, X;
  wire [3:0] score_counter_1_out_3, score_counter_2_out_3;
  wire [5:0] tavolo_di_gioco_1__1_1, tavolo_di_gioco_1__1_2, tavolo_di_gioco_1__1_3, tavolo_di_gioco_1__2_1,
       tavolo_di_gioco_1__2_2, tavolo_di_gioco_1__2_3, tavolo_di_gioco_1__3_1, tavolo_di_gioco_1__3_2,
       tavolo_di_gioco_1__3_3, tavolo_di_gioco_1__4_1, tavolo_di_gioco_1__4_2, tavolo_di_gioco_1__4_3,
       tavolo_di_gioco_1__5_1, tavolo_di_gioco_1__5_2, tavolo_di_gioco_1__5_3, tavolo_di_gioco_1__6_1,
       tavolo_di_gioco_1__6_2, tavolo_di_gioco_1__6_3, tavolo_di_gioco_1__7_1, tavolo_di_gioco_1__7_2,
       tavolo_di_gioco_1__7_3, tavolo_di_gioco_1__8_1, tavolo_di_gioco_1__8_2, tavolo_di_gioco_1__8_3,
       tavolo_di_gioco_1__9_1, tavolo_di_gioco_1__9_2, tavolo_di_gioco_1__9_3, vittoria_1_out_3,
       vittoria_1_out_4, vittoria_1_out_5, vittoria_1_out_6, vittoria_1_out_7, vittoria_1_out_8,
       vittoria_1_out_9, vittoria_1_out_10, vittoria_1_out_11, vittoria_1_out_12, vittoria_1_out_13,
       vittoria_1_out_14, vittoria_1_out_15, vittoria_1_out_16, vittoria_1_out_17, vittoria_1_out_18,
       vittoria_1_out_19, vittoria_1_out_20, vittoria_1_out_21, vittoria_1_out_22, vittoria_1_out_23,
       vittoria_1_out_24, vittoria_1_out_25, vittoria_1_out_26, vittoria_1_out_27, vittoria_1_out_28;

  Button button_1 (.out(button_1_out));
  Button button_2 (.out(button_2_out));
  Button button_3 (.out(button_3_out));
  Button button_4 (.out(button_4_out));
  Button button_5 (.out(button_5_out));
  Button button_6 (.out(button_6_out));
  Button START_RESET (.out(START_RESET_out));
  Button button_7 (.out(button_7_out));
  Button button_8 (.out(button_8_out));
  Button button_9 (.out(button_9_out));
  DotMatrix #(.matrixrows(6)) dotmatrix_1 (
    .col0(vittoria_1_out_3), .col1(vittoria_1_out_4), .col2(vittoria_1_out_5), .col3(vittoria_1_out_4),
    .col4(vittoria_1_out_3));
  Tavolo_di_gioco tavolo_di_gioco_1 (
    ._1(button_1_out), ._2(button_4_out), ._3(button_7_out), ._4(button_2_out), ._5(button_5_out),
    ._6(button_8_out), ._7(button_3_out), ._8(button_6_out), ._9(button_9_out),
    .START_RESET(START_RESET_out), ._1_1(tavolo_di_gioco_1__1_1), ._1_2(tavolo_di_gioco_1__1_2),
    ._1_3(tavolo_di_gioco_1__1_3), ._2_1(tavolo_di_gioco_1__2_1), ._2_2(tavolo_di_gioco_1__2_2),
    ._2_3(tavolo_di_gioco_1__2_3), ._3_1(tavolo_di_gioco_1__3_1), ._3_2(tavolo_di_gioco_1__3_2),
    ._3_3(tavolo_di_gioco_1__3_3), ._4_1(tavolo_di_gioco_1__4_1), ._4_2(tavolo_di_gioco_1__4_2),
    ._4_3(tavolo_di_gioco_1__4_3), ._5_1(tavolo_di_gioco_1__5_1), ._5_2(tavolo_di_gioco_1__5_2),
    ._5_3(tavolo_di_gioco_1__5_3), ._6_1(tavolo_di_gioco_1__6_1), ._6_2(tavolo_di_gioco_1__6_2),
    ._6_3(tavolo_di_gioco_1__6_3), ._7_1(tavolo_di_gioco_1__7_1), ._7_2(tavolo_di_gioco_1__7_2),
    ._7_3(tavolo_di_gioco_1__7_3), ._8_1(tavolo_di_gioco_1__8_1), ._8_2(tavolo_di_gioco_1__8_2),
    ._8_3(tavolo_di_gioco_1__8_3), ._9_1(tavolo_di_gioco_1__9_1), ._9_2(tavolo_di_gioco_1__9_2),
    ._9_3(tavolo_di_gioco_1__9_3), .X_wins(X), .O_wins(O));
  DotMatrix #(.matrixcols(23), .matrixrows(6)) dotmatrix_2 (
    .col0(vittoria_1_out_28), .col1(vittoria_1_out_27), .col2(vittoria_1_out_26), .col3(vittoria_1_out_25),
    .col4(vittoria_1_out_24), .col5(vittoria_1_out_23), .col6(vittoria_1_out_22), .col7(vittoria_1_out_21),
    .col8(vittoria_1_out_20), .col9(vittoria_1_out_19), .col10(vittoria_1_out_18), .col11(vittoria_1_out_17),
    .col12(vittoria_1_out_16), .col13(vittoria_1_out_15), .col14(vittoria_1_out_14),
    .col15(vittoria_1_out_13), .col16(vittoria_1_out_12), .col17(vittoria_1_out_11),
    .col18(vittoria_1_out_10), .col19(vittoria_1_out_9), .col20(vittoria_1_out_8), .col21(vittoria_1_out_7),
    .col22(vittoria_1_out_6));
  Vittoria vittoria_1 (
    .X(X), .O(O), .out_3(vittoria_1_out_3), .out_4(vittoria_1_out_4), .out_5(vittoria_1_out_5),
    .out_6(vittoria_1_out_6), .out_7(vittoria_1_out_7), .out_8(vittoria_1_out_8), .out_9(vittoria_1_out_9),
    .out_10(vittoria_1_out_10), .out_11(vittoria_1_out_11), .out_12(vittoria_1_out_12),
    .out_13(vittoria_1_out_13), .out_14(vittoria_1_out_14), .out_15(vittoria_1_out_15),
    .out_16(vittoria_1_out_16), .out_17(vittoria_1_out_17), .out_18(vittoria_1_out_18),
    .out_19(vittoria_1_out_19), .out_20(vittoria_1_out_20), .out_21(vittoria_1_out_21),
    .out_22(vittoria_1_out_22), .out_23(vittoria_1_out_23), .out_24(vittoria_1_out_24),
    .out_25(vittoria_1_out_25), .out_26(vittoria_1_out_26), .out_27(vittoria_1_out_27),
    .out_28(vittoria_1_out_28));
  DotMatrix #(.matrixrows(6)) dotmatrix_3 (
    .col0(tavolo_di_gioco_1__1_1), .col1(tavolo_di_gioco_1__1_2), .col2(tavolo_di_gioco_1__1_3),
    .col3(tavolo_di_gioco_1__1_2), .col4(tavolo_di_gioco_1__1_1));
  DotMatrix #(.matrixrows(6)) dotmatrix_4 (
    .col0(tavolo_di_gioco_1__4_1), .col1(tavolo_di_gioco_1__4_2), .col2(tavolo_di_gioco_1__4_3),
    .col3(tavolo_di_gioco_1__4_2), .col4(tavolo_di_gioco_1__4_1));
  DotMatrix #(.matrixrows(6)) dotmatrix_5 (
    .col0(tavolo_di_gioco_1__7_1), .col1(tavolo_di_gioco_1__7_2), .col2(tavolo_di_gioco_1__7_3),
    .col3(tavolo_di_gioco_1__7_2), .col4(tavolo_di_gioco_1__7_1));
  DotMatrix #(.matrixrows(6)) dotmatrix_6 (
    .col0(tavolo_di_gioco_1__2_1), .col1(tavolo_di_gioco_1__2_2), .col2(tavolo_di_gioco_1__2_3),
    .col3(tavolo_di_gioco_1__2_2), .col4(tavolo_di_gioco_1__2_1));
  DotMatrix #(.matrixrows(6)) dotmatrix_7 (
    .col0(tavolo_di_gioco_1__5_1), .col1(tavolo_di_gioco_1__5_2), .col2(tavolo_di_gioco_1__5_3),
    .col3(tavolo_di_gioco_1__5_2), .col4(tavolo_di_gioco_1__5_1));
  DotMatrix #(.matrixrows(6)) dotmatrix_8 (
    .col0(tavolo_di_gioco_1__8_1), .col1(tavolo_di_gioco_1__8_2), .col2(tavolo_di_gioco_1__8_3),
    .col3(tavolo_di_gioco_1__8_2), .col4(tavolo_di_gioco_1__8_1));
  DotMatrix #(.matrixrows(6)) dotmatrix_9 (
    .col0(tavolo_di_gioco_1__3_1), .col1(tavolo_di_gioco_1__3_2), .col2(tavolo_di_gioco_1__3_3),
    .col3(tavolo_di_gioco_1__3_2), .col4(tavolo_di_gioco_1__3_1));
  DotMatrix #(.matrixrows(6)) dotmatrix_10 (
    .col0(tavolo_di_gioco_1__6_1), .col1(tavolo_di_gioco_1__6_2), .col2(tavolo_di_gioco_1__6_3),
    .col3(tavolo_di_gioco_1__6_2), .col4(tavolo_di_gioco_1__6_1));
  DotMatrix #(.matrixrows(6)) dotmatrix_11 (
    .col0(tavolo_di_gioco_1__9_1), .col1(tavolo_di_gioco_1__9_2), .col2(tavolo_di_gioco_1__9_3),
    .col3(tavolo_di_gioco_1__9_2), .col4(tavolo_di_gioco_1__9_1));
  Hex_Digit_Display hex_digit_display_1 (.value(score_counter_1_out_3));  // open: dp
  Score_Counter score_counter_1 (.IN(X), .out_3(score_counter_1_out_3), .RESET(RESET_SCORE_out));
  Button RESET_SCORE (.out(RESET_SCORE_out));
  Hex_Digit_Display hex_digit_display_2 (.value(score_counter_2_out_3));  // open: dp
  Score_Counter score_counter_2 (.IN(O), .out_3(score_counter_2_out_3), .RESET(RESET_SCORE_out));

  // Notes on the sheet:
  //   SCORE
  //   X
  //   O
endmodule

module Tavolo_di_gioco (
  input  _1,
  input  _2,
  input  _3,
  input  _4,
  input  _5,
  input  _6,
  input  _7,
  input  _8,
  input  _9,
  input  START_RESET,
  output [5:0] _1_1,
  output [5:0] _1_2,
  output [5:0] _1_3,
  output [5:0] _2_1,
  output [5:0] _2_2,
  output [5:0] _2_3,
  output [5:0] _3_1,
  output [5:0] _3_2,
  output [5:0] _3_3,
  output [5:0] _4_1,
  output [5:0] _4_2,
  output [5:0] _4_3,
  output X_wins,
  output O_wins,
  output [5:0] _5_1,
  output [5:0] _5_2,
  output [5:0] _5_3,
  output [5:0] _6_1,
  output [5:0] _6_2,
  output [5:0] _6_3,
  output [5:0] _7_1,
  output [5:0] _7_2,
  output [5:0] _7_3,
  output [5:0] _8_1,
  output [5:0] _8_2,
  output [5:0] _8_3,
  output [5:0] _9_1,
  output [5:0] _9_2,
  output [5:0] _9_3
);

  wire and_1_out, and_2_out, and_3_out, and_4_out, and_5_out, and_6_out, and_7_out, and_8_out, and_9_out,
       and_10_out, and_11_out, and_12_out, and_13_out, and_14_out, and_15_out, and_16_out, t_ff_1_q, XOR1,
       XOR2, XOR3, XOR4, XOR5, XOR6, XOR7, XOR8, XOR9, xor_1_out;

  T_Flip_Flop t_ff_1 (.clk(START_RESET), .T(1'b1), .Q(t_ff_1_q), .preset(1'b0), .reset(1'b0), .en(1'b1));  // open: Qn
  Selezione selezione_1 (.IN(_1), .C(xor_1_out), .L1(_1_2[4]), .L2(_1_1[4]), .RESET(START_RESET), .XOR(XOR1));
  Selezione selezione_2 (.IN(_2), .C(xor_1_out), .L1(_2_2[4]), .L2(_2_1[4]), .RESET(START_RESET), .XOR(XOR2));
  Selezione selezione_3 (.IN(_3), .C(xor_1_out), .L1(_3_2[4]), .L2(_3_1[4]), .RESET(START_RESET), .XOR(XOR3));
  Selezione selezione_4 (.IN(_4), .C(xor_1_out), .L1(_4_2[4]), .L2(_4_1[4]), .RESET(START_RESET), .XOR(XOR4));
  Selezione selezione_5 (.IN(_5), .C(xor_1_out), .L1(_5_2[4]), .L2(_5_1[4]), .RESET(START_RESET), .XOR(XOR5));
  Selezione selezione_6 (.IN(_6), .C(xor_1_out), .L1(_6_2[4]), .L2(_6_1[4]), .RESET(START_RESET), .XOR(XOR6));
  Selezione selezione_7 (.IN(_7), .C(xor_1_out), .L1(_7_2[4]), .L2(_7_1[4]), .RESET(START_RESET), .XOR(XOR7));
  Selezione selezione_8 (.IN(_8), .C(xor_1_out), .L1(_8_2[4]), .L2(_8_1[4]), .RESET(START_RESET), .XOR(XOR8));
  Selezione selezione_9 (.IN(_9), .C(xor_1_out), .L1(_9_2[4]), .L2(_9_1[4]), .RESET(START_RESET), .XOR(XOR9));
  or or_1 (_1_1[5], _1_2[4], _1_1[4]);
  or or_2 (_2_1[5], _2_2[4], _2_1[4]);
  or or_3 (_3_1[5], _3_2[4], _3_1[4]);
  or or_4 (_4_1[5], _4_2[4], _4_1[4]);
  or or_5 (_5_1[5], _5_2[4], _5_1[4]);
  or or_6 (_6_1[5], _6_2[4], _6_1[4]);
  or or_7 (_7_1[5], _7_2[4], _7_1[4]);
  or or_8 (_8_1[5], _8_2[4], _8_1[4]);
  or or_9 (_9_1[5], _9_2[4], _9_1[4]);
  xor xor_1 (xor_1_out, XOR1, XOR2, XOR3, XOR4, XOR5, XOR6, XOR7, XOR8, XOR9, t_ff_1_q);
  and and_1 (and_1_out, _1_2[4], _4_2[4], _7_2[4]);
  and and_2 (and_2_out, _1_2[4], _2_2[4], _3_2[4]);
  and and_3 (and_3_out, _1_1[4], _2_1[4], _3_1[4]);
  and and_4 (and_4_out, _1_2[4], _5_2[4], _9_2[4]);
  and and_5 (and_5_out, _3_1[4], _6_1[4], _9_1[4]);
  and and_6 (and_6_out, _2_2[4], _5_2[4], _8_2[4]);
  and and_7 (and_7_out, _1_1[4], _4_1[4], _7_1[4]);
  and and_8 (and_8_out, _3_1[4], _5_1[4], _7_1[4]);
  and and_9 (and_9_out, _4_2[4], _5_2[4], _6_2[4]);
  and and_10 (and_10_out, _4_1[4], _5_1[4], _6_1[4]);
  and and_11 (and_11_out, _2_1[4], _5_1[4], _8_1[4]);
  and and_12 (and_12_out, _3_2[4], _5_2[4], _7_2[4]);
  and and_13 (and_13_out, _1_1[4], _5_1[4], _9_1[4]);
  and and_14 (and_14_out, _7_2[4], _8_2[4], _9_2[4]);
  and and_15 (and_15_out, _7_1[4], _8_1[4], _9_1[4]);
  and and_16 (and_16_out, _3_2[4], _6_2[4], _9_2[4]);
  or or_10 (X_wins, and_16_out, and_14_out, and_12_out, and_9_out, and_6_out, and_4_out, and_2_out, and_1_out);
  or or_11 (O_wins, and_3_out, and_5_out, and_7_out, and_8_out, and_10_out, and_11_out, and_13_out, and_15_out);

  assign _1_1[3:0] = {{3{_1_1[4]}}, _1_1[5]};
  assign {_1_2[5], _1_2[3:0]} = {_1_1[4], 2'b00, _1_2[4], _1_1[4]};
  assign _1_3 = {_1_1[4], 1'b0, {2{_1_2[4]}}, 1'b0, _1_1[4]};
  assign _2_1[3:0] = {{3{_2_1[4]}}, _2_1[5]};
  assign {_2_2[5], _2_2[3:0]} = {_2_1[4], 2'b00, _2_2[4], _2_1[4]};
  assign _2_3 = {_2_1[4], 1'b0, {2{_2_2[4]}}, 1'b0, _2_1[4]};
  assign _3_1[3:0] = {{3{_3_1[4]}}, _3_1[5]};
  assign {_3_2[5], _3_2[3:0]} = {_3_1[4], 2'b00, _3_2[4], _3_1[4]};
  assign _3_3 = {_3_1[4], 1'b0, {2{_3_2[4]}}, 1'b0, _3_1[4]};
  assign _4_1[3:0] = {{3{_4_1[4]}}, _4_1[5]};
  assign {_4_2[5], _4_2[3:0]} = {_4_1[4], 2'b00, _4_2[4], _4_1[4]};
  assign _4_3 = {_4_1[4], 1'b0, {2{_4_2[4]}}, 1'b0, _4_1[4]};
  assign _5_1[3:0] = {{3{_5_1[4]}}, _5_1[5]};
  assign {_5_2[5], _5_2[3:0]} = {_5_1[4], 2'b00, _5_2[4], _5_1[4]};
  assign _5_3 = {_5_1[4], 1'b0, {2{_5_2[4]}}, 1'b0, _5_1[4]};
  assign _6_1[3:0] = {{3{_6_1[4]}}, _6_1[5]};
  assign {_6_2[5], _6_2[3:0]} = {_6_1[4], 2'b00, _6_2[4], _6_1[4]};
  assign _6_3 = {_6_1[4], 1'b0, {2{_6_2[4]}}, 1'b0, _6_1[4]};
  assign _7_1[3:0] = {{3{_7_1[4]}}, _7_1[5]};
  assign {_7_2[5], _7_2[3:0]} = {_7_1[4], 2'b00, _7_2[4], _7_1[4]};
  assign _7_3 = {_7_1[4], 1'b0, {2{_7_2[4]}}, 1'b0, _7_1[4]};
  assign _8_1[3:0] = {{3{_8_1[4]}}, _8_1[5]};
  assign {_8_2[5], _8_2[3:0]} = {_8_1[4], 2'b00, _8_2[4], _8_1[4]};
  assign _8_3 = {_8_1[4], 1'b0, {2{_8_2[4]}}, 1'b0, _8_1[4]};
  assign _9_1[3:0] = {{3{_9_1[4]}}, _9_1[5]};
  assign {_9_2[5], _9_2[3:0]} = {_9_1[4], 2'b00, _9_2[4], _9_1[4]};
  assign _9_3 = {_9_1[4], 1'b0, {2{_9_2[4]}}, 1'b0, _9_1[4]};

  // Other names for the same wires on the sheet: X1 = _1_2[4]; O1 = _1_1[4]; X2 = _2_2[4]; O2 = _2_1[4]; X3 = _3_2[4];
  //   O3 = _3_1[4]; X4 = _4_2[4]; O4 = _4_1[4]; X5 = _5_2[4]; O5 = _5_1[4]; X6 = _6_2[4]; O6 = _6_1[4]; X7 = _7_2[4];
  //   O7 = _7_1[4]; X8 = _8_2[4]; O8 = _8_1[4]; X9 = _9_2[4]; O9 = _9_1[4]
endmodule

module Selezione (
  input  IN,
  input  C,
  input  RESET,
  output L1,
  output XOR,
  output L2
);

  wire and_1_out, and_2_out, demultiplexer_1_out0, demultiplexer_1_out1, latch_sr_3_nq;

  Demultiplexer #(.enable("false")) demultiplexer_1 (
    .out0(demultiplexer_1_out0), .out1(demultiplexer_1_out1), .in(IN), .sel(C));
  and and_1 (and_1_out, demultiplexer_1_out0, latch_sr_3_nq);
  and and_2 (and_2_out, demultiplexer_1_out1, latch_sr_3_nq);
  Latch_SR latch_sr_1 (.S(and_1_out), .R(RESET), .Q(L1));  // open: nQ
  Latch_SR latch_sr_2 (.S(and_2_out), .R(RESET), .Q(L2));  // open: nQ
  or or_1 (XOR, L1, L2);
  Latch_SR latch_sr_3 (.S(XOR), .R(RESET), .nQ(latch_sr_3_nq));  // open: Q
endmodule

module Score_Counter (
  input  IN,
  input  RESET,
  output [3:0] out_3
);

  Counter #(.width(4), .max('hf), .ongoal("stay")) counter_1 (
    .D(4'b0001), .count(IN), .Q(out_3), .clk(IN), .clr(RESET));  // open: load, carry
endmodule

module Vittoria (
  input  X,
  input  O,
  output [5:0] out_3,
  output [5:0] out_4,
  output [5:0] out_5,
  output [5:0] out_6,
  output [5:0] out_7,
  output [5:0] out_8,
  output [5:0] out_9,
  output [5:0] out_10,
  output [5:0] out_11,
  output [5:0] out_12,
  output [5:0] out_13,
  output [5:0] out_14,
  output [5:0] out_15,
  output [5:0] out_16,
  output [5:0] out_17,
  output [5:0] out_18,
  output [5:0] out_19,
  output [5:0] out_20,
  output [5:0] out_21,
  output [5:0] out_22,
  output [5:0] out_23,
  output [5:0] out_24,
  output [5:0] out_25,
  output [5:0] out_26,
  output [5:0] out_27,
  output [5:0] out_28
);

  or or_1 (out_7[5], X, O);
  or or_2 (out_3[5], X, O);

  assign out_3[4:0] = {{4{O}}, out_3[5]};
  assign out_4 = {O, X, 2'b00, X, O};
  assign out_5 = {O, 1'b0, {2{X}}, 1'b0, O};
  assign out_6 = {6{1'b0}};
  assign out_7[4:0] = {{3{out_7[5]}}, 1'b0, out_7[5]};
  assign out_8 = {6{1'b0}};
  assign out_9 = {out_7[5], 3'b000, out_7[5], 1'b0};
  assign out_10 = {out_7[5], 1'b0, {2{out_7[5]}}, 1'b0, out_7[5]};
  assign out_11 = {out_7[5], 1'b0, {2{out_7[5]}}, 1'b0, out_7[5]};
  assign out_12 = {{2{out_7[5]}}, 3'b000, out_7[5]};
  assign out_13 = {6{1'b0}};
  assign out_14 = {6{out_7[5]}};
  assign out_15 = {3'b000, {3{out_7[5]}}};
  assign out_16 = {1'b0, {2{out_7[5]}}, 3'b000};
  assign out_17 = {6{out_7[5]}};
  assign out_18 = {6{1'b0}};
  assign out_19 = {6{out_7[5]}};
  assign out_20 = {6{1'b0}};
  assign out_21 = {{3{out_7[5]}}, 3'b000};
  assign out_22 = {3'b000, {3{out_7[5]}}};
  assign out_23 = {4'b0000, out_7[5], 1'b0};
  assign out_24 = {3'b000, out_7[5], 2'b00};
  assign out_25 = {4'b0000, out_7[5], 1'b0};
  assign out_26 = {3'b000, {3{out_7[5]}}};
  assign out_27 = {{3{out_7[5]}}, 3'b000};
  assign out_28 = {6{1'b0}};
endmodule

module Latch_SR (
  input  S,
  input  R,
  output Q,
  output nQ
);

  nor nor_1 (nQ, S, Q);
  nor nor_2 (Q, nQ, R);
endmodule
